# Fritzing sketch BinKun V1.0 (saved by Fritzing 0.9.4)
breadboards: 1
perfboards: 1

parts:
  Raspberry_Pi_1 = Raspberry Pi 3 [part_number=RPI-3-V1.2]
  M1 = DC Motor
  Bat1 = battery_holder_dual_18650 [part_number=TBH-18650-2A-P]
  M2 = DC Motor
  Part1 = Adafruit T-Cobbler Plus [part_number="Adafruit #1989 and #2028"]
  Part3 = Motor Driver 1A Dual TB6612FNG
  HC-SR04_Sensor_1 = HC-SR04 Ultrasonic Distance Sensor [part_number=R]
  HC-SR04_Sensor_2 = HC-SR04 Ultrasonic Distance Sensor [part_number=F]
  HC-SR04_Sensor_3 = HC-SR04 Ultrasonic Distance Sensor [part_number=L]
  HC-SR04_Sensor_4 = HC-SR04 Ultrasonic Distance Sensor [part_number=B]
  Part4 = TXB0108 8-channel Bi-directional Logic Level Converter

nets:
  3V3: Raspberry_Pi_1.3v3, Raspberry_Pi_1.3V3, Part1.+3.3V, Part4.OE, Part4.VCCA
  N1: Raspberry_Pi_1.GPIO2, Part1.SDA
  N2: Raspberry_Pi_1.GPIO3, Part1.SCL
  N3: Raspberry_Pi_1.GPIO4, Part1.GPIO4
  N4: Raspberry_Pi_1.GPIO17, Part1.GPIO17, Part3.BIN2
  N5: Raspberry_Pi_1.GPIO27, Part1.GPIO27
  N6: Raspberry_Pi_1.GPIO22, Part1.GPIO22, HC-SR04_Sensor_1.TRIG
  N7: Raspberry_Pi_1.GPIO10, Part1.MOSI
  N8: Raspberry_Pi_1.GPIO9, Part1.MISO
  N9: Raspberry_Pi_1.GPIO11, Part1.SCLK
  N10: Raspberry_Pi_1.ID_SD, Part1.EEDAT
  N11: Raspberry_Pi_1.GPIO5, Part1.GPIO5, HC-SR04_Sensor_2.TRIG
  N12: Raspberry_Pi_1.GPIO6, Part1.GPIO6, Part3.AIN1
  N13: Raspberry_Pi_1.GPIO13, Part1.GPIO13, Part3.BIN1
  N14: Raspberry_Pi_1.GPIO19, Part1.GPIO19, Part3.AIN2
  N15: Raspberry_Pi_1.GPIO26, Part1.GPIO26, Part3.STBY
  N16: Raspberry_Pi_1.GPIO21, Part1.GPIO21, HC-SR04_Sensor_4.TRIG
  N17: Raspberry_Pi_1.GPIO20, Part1.GPIO20, Part4.A4
  N18: Raspberry_Pi_1.GPIO16, Part1.GPIO16, Part4.A5
  N19: Raspberry_Pi_1.GPIO12, Part1.GPIO12, Part4.A6
  GND: Raspberry_Pi_1.GND, Bat1.+#0, Part1.GND, Part3.GND, HC-SR04_Sensor_1.GND, HC-SR04_Sensor_2.GND, HC-SR04_Sensor_3.GND, HC-SR04_Sensor_4.GND, Part4.GND
  N20: Raspberry_Pi_1.ID_SC, Part1.EECLK
  N21: Raspberry_Pi_1.GPIO7, Part1.CE1
  N22: Raspberry_Pi_1.GPIO8, Part1.CE0
  N23: Raspberry_Pi_1.GPIO25, Part1.GPIO25, Part4.A7
  N24: Raspberry_Pi_1.GPIO24, Part1.GPIO24, HC-SR04_Sensor_3.TRIG
  N25: Raspberry_Pi_1.GPIO23, Part1.GPIO23
  N26: Raspberry_Pi_1.GPIO18, Part1.GPIO18
  N27: Raspberry_Pi_1.GPIO15, Part1.RXD
  N28: Raspberry_Pi_1.GPIO14, Part1.TXD
  VCC: Raspberry_Pi_1.5V, Part1.+5V, Part3.VCC, HC-SR04_Sensor_1.VCC, HC-SR04_Sensor_2.VCC, HC-SR04_Sensor_3.VCC, HC-SR04_Sensor_4.VCC, Part4.VCCB
  N29: M1.pin_1, Part3.A02
  N30: M1.pin_2, Part3.A01
  N31: Bat1.+#1, Bat1.+#3
  N32: Bat1.+#2, Part3.VM
  N33: M2.pin_1, Part3.B02
  N34: M2.pin_2, Part3.B01
  N35: HC-SR04_Sensor_1.ECHO, Part4.B7
  N36: HC-SR04_Sensor_2.ECHO, Part4.B6
  N37: HC-SR04_Sensor_3.ECHO, Part4.B5
  N38: HC-SR04_Sensor_4.ECHO, Part4.B4

custom parts:
  battery_holder_dual_18650: TBH-18650-2A-P dual 18650 battery holder.
  Adafruit T-Cobbler Plus: The Raspberry Pi has landed on the Maker World like a 40-GPIO pinned, quad-USB ported, credit card sized bomb of DIY joy. And while you can use most of our great Model B accessories by hooking up our downgrade cable, its probably a good time to upgrade your set up and accessorize using all of the 40 pins. That's why we now carry the Assembled Adafruit Pi T-Cobbler Plus - Breakout + Cable for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
  TXB0108 8-channel Bi-directional Logic Level Converter: Because the Arduino (and Basic Stamp) are 5V devices, and most modern sensors, displays, flash cards and modes are 3.3V-only, many makers find that they need to perform level shifting/conversion to protect the 3.3V device from 5V. Although one can use resistors to make a divider, for high speed transfers, the resistors can add a lot of slew and cause havoc that is tough to debug. For that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
