# Fritzing sketch BinKun V2.0 (saved by Fritzing 0.9.4)
breadboards: 1

parts:
  Part1 = Arduino Nano (Rev3.0) (ICSP)
  HC-SR04_Sensor_1 = HC-SR04 Ultrasonic Distance Sensor
  HC-SR04_Sensor_2 = HC-SR04 Ultrasonic Distance Sensor
  HC-SR04_Sensor_3 = HC-SR04 Ultrasonic Distance Sensor
  HC-SR04_Sensor_4 = HC-SR04 Ultrasonic Distance Sensor
  J1 = Raspberry Pi Header 40pin [package=THT]
  Part2 = Adafruit Motor/Stepper/Servo Shield [part_number="Adafruit #1438"]
  Bat1 = battery_holder_dual_18650 [part_number=TBH-18650-2A-P]
  M1 = DC Motor
  M2 = DC Motor

nets:
  GND: Part1.GND, HC-SR04_Sensor_1.GND, HC-SR04_Sensor_2.GND, HC-SR04_Sensor_3.GND, HC-SR04_Sensor_4.GND
  N1: Part1.D3, HC-SR04_Sensor_1.TRIG, HC-SR04_Sensor_2.TRIG, HC-SR04_Sensor_3.TRIG, HC-SR04_Sensor_4.TRIG
  N2: Part1.D4, HC-SR04_Sensor_2.ECHO
  N3: Part1.D5, HC-SR04_Sensor_1.ECHO
  N4: Part1.D6, HC-SR04_Sensor_3.ECHO
  N5: Part1.D7, HC-SR04_Sensor_4.ECHO
  VCC: Part1.5V, HC-SR04_Sensor_1.VCC, HC-SR04_Sensor_2.VCC, HC-SR04_Sensor_3.VCC, HC-SR04_Sensor_4.VCC
  N6: Part1.A5, J1.IO3
  N7: Part1.A4, J1.GPIO2
  3V3: J1.3V3, Part2.+3V3
  GND_2: J1.GND, Part2.AD4/SDA, Part2.GND, Bat1.+#0
  N8: J1.IO7, Part2.AD5/SCL
  N9: Part2.M3A, M2.pin_2
  N10: Part2.M3B, M2.pin_1
  N11: Part2.M4B, M1.pin_2
  N12: Part2.M4A, M1.pin_1
  N13: Part2.VMOTOR, Bat1.+#2
  N14: Bat1.+#1, Bat1.+#3

custom parts:
  Raspberry Pi Header 40pin: Raspberry Pi 40 pin header - for creating your own shields. (Mar 2020, bb: make breadboard friendly (.4in pin spacing) and add labels. Schematic add labels. PCB make oblong pins to allow routing traces between the pins.)
  Adafruit Motor/Stepper/Servo Shield: The original Adafruit Motorshield kit is one of our most beloved kits, which is why we decided to make something even better. We have upgraded the shield kit to make the bestest, easiest way to drive DC and Stepper motors. This shield will make quick work of your next robotics project! We kept the ability to drive up to 4 DC motors or 2 stepper motors, but added many improvements: Instead of a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
  battery_holder_dual_18650: TBH-18650-2A-P dual 18650 battery holder.
